# Fritzing sketch 808Drum3 (saved by Fritzing 0.9.2b)
breadboards: 1

parts:
  IC1 = DIP - 8 pins [chip_label=LM358 package="DIP (Dual Inline) [THT]"]
  VCC2 = Battery block 9V  # not connected
  R2 = Resistor [tolerance=±5% resistance=10k package=THT]
  R4 = Resistor [tolerance=±5% resistance=10k package=THT]
  R10 = Resistor [tolerance=±5% resistance=10k package=THT]
  R11 = Resistor [tolerance=±5% resistance=10k package=THT]
  R12 = Resistor [tolerance=±5% resistance=10k package=THT]
  C5 = Electrolytic Capacitor [capacitance=1000μF package="1010 [SMD, electrolytic]"]
  D4 = Rectifier Diode [part_number=1N4001 package="Melf DO-213 AB [SMD]"]
  C6 = Ceramic Capacitor [capacitance=100nF package="100 mil [THT, multilayer]"]
  R13 = Resistor [tolerance=±5% resistance=220 package=THT]
  R14 = Resistor [tolerance=±5% resistance=4.7k package=THT]
  C9 = Ceramic Capacitor [capacitance=100nF package="100 mil [THT, multilayer]"]
  C10 = Ceramic Capacitor [capacitance=100nF package="100 mil [THT, multilayer]"]
  R18 = Resistor [tolerance=±5% resistance=220 package=THT]
  R20 = Resistor [tolerance=±5% resistance=1M package=THT]
  C12 = Ceramic Capacitor [capacitance=100nF package="100 mil [THT, multilayer]"]
  R26 = Resistor [tolerance=±5% resistance=470k package=THT]
  R27 = Resistor [tolerance=±5% resistance=470k package=THT]
  R28 = Resistor [tolerance=±5% resistance=47k package=THT]
  R19 = Rotary Potentiometer (Large) [maximum_resistance=100kΩ package=THT]
  R22 = Rotary Potentiometer (Large) [maximum_resistance=100kΩ package=THT]

nets:
  N1: IC1.pin1, IC1.pin2, R4.Pin_1, R12.Pin_1, R19.leg1, R22.leg1
  N2: IC1.pin3, R2.Pin_1, R4.Pin_0
  N3: IC1.pin4, R10.Pin_1, R13.Pin_1
  N4: IC1.pin5, R12.Pin_0, D4.cathode
  N5: IC1.pin6, C10.1, R20.Pin_1, R26.Pin_1
  N6: IC1.pin7, R14.Pin_1, C9.0, R20.Pin_0, R27.Pin_0
  N7: IC1.pin8, R2.Pin_0
  N8: R10.Pin_0, C6.0
  N9: R11.Pin_0, D4.anode, C6.1
  N10: C5.-, R13.Pin_0
  N11: C5.+, R14.Pin_0
  N12: C9.1, C10.0, R18.Pin_1
  N13: R18.Pin_0, R19.wiper
  N14: C12.0, R26.Pin_0, R27.Pin_1
  N15: C12.1, R28.Pin_1
  N16: R28.Pin_0, R22.wiper

notes:
  0V
  4.5V
  9V
  Trigger input
  Sound output
  Frequency
  Decay time

custom parts:
  DIP - 8 pins: A DIP stand-in part for whatever IC you want. With 8 pins on a 300mil dual inline package (DIP) footprint.
